// Logisim project RISC-8bit-processor.circ as structural Verilog: 4 circuits, main circuit main
module main (
);

  wire alu_1_overflow, alu_1_zero, clock_1_out, not_1_out, not_2_out, OVERFLOW_q, RESET_out, uc_1_ac,
       uc_1_ir, uc_1_load, \uc_1_mod__endereçamento , uc_1_pc, uc_1_pc_rst, uc_1_r_w, uc_1_ram, Z_q;
  wire [2:0] uc_1_opcode;
  wire [3:0] \alu_1_saída , multiplexer_1_out, PC_q, ram_1_data, register_1_q, uc_1_endereco, uc_1_operando;
  wire [7:0] IR_q, rom_1_data;

  Counter #(.width(4), .max('hf)) PC (
    .load(uc_1_load), .D(uc_1_endereco), .count(not_1_out), .Q(PC_q), .clk(uc_1_pc), .clr(uc_1_pc_rst));  // open: carry
  not not_1 (not_1_out, uc_1_load);
  Register #(.trigger("high")) IR (.D(rom_1_data), .Q(IR_q), .clk(uc_1_ir));  // open: en, clr
  ROM #(.addrWidth(4)) rom_1 (.addr(PC_q), .data(rom_1_data));  // open: sel
  UC uc_1 (
    .OpCode(uc_1_opcode), .\Mod__Endereçamento (\uc_1_mod__endereçamento ), .\Instrução (IR_q),
    .Operando(uc_1_operando), .IR(uc_1_ir), .PC(uc_1_pc), .AC(uc_1_ac), .RAM(uc_1_ram), .CLK(clock_1_out),
    .RST(RESET_out), .PC_RST(uc_1_pc_rst), .R_W(uc_1_r_w), .Z(Z_q), .C(OVERFLOW_q), .Load(uc_1_load),
    .Endereco(uc_1_endereco));
  Clock clock_1 (.out(clock_1_out));
  Button RESET (.out(RESET_out));
  Multiplexer #(.width(4), .enable("false")) multiplexer_1 (
    .in0(uc_1_operando), .in1(ram_1_data), .out(multiplexer_1_out), .sel(\uc_1_mod__endereçamento ));
  ALU alu_1 (
    .A(register_1_q), .B(multiplexer_1_out), .OVERFLOW(alu_1_overflow), .DIR(\uc_1_mod__endereçamento ),
    .\OPERAÇÃO (uc_1_opcode), .ZERO(alu_1_zero), .\SAÍDA (\alu_1_saída ));
  Register #(.width(4)) register_1 (.D(\alu_1_saída ), .Q(register_1_q), .clk(uc_1_ac));  // open: en, clr
  Register #(.width(1)) Z (.D(alu_1_zero), .Q(Z_q), .clk(uc_1_ac));  // open: en, clr
  Register #(.width(1)) OVERFLOW (.D(alu_1_overflow), .Q(OVERFLOW_q), .clk(uc_1_ac));  // open: en, clr
  RAM #(.addrWidth(4), .dataWidth(4)) ram_1 (
    .addr(uc_1_operando), .data(ram_1_data), .clk(uc_1_ram), .ld(uc_1_r_w));  // open: sel, clr
  assign ram_1_data = not_2_out ? register_1_q : 4'bz;  // Controlled_Buffer controlled_buffer_1
  not not_2 (not_2_out, uc_1_r_w);

  // Notes on the sheet:
  //   contents of rom_1 (hex, n*v repeats v):
  //   0 f0 1 f1 10 31 f2 11 f0 12 f1 e4 7 a 17 11
endmodule

module ALU (
  input  [3:0] A,
  input  [3:0] B,
  input  DIR,
  input  [2:0] \OPERAÇÃO ,
  output OVERFLOW,
  output [3:0] \SAÍDA ,
  output ZERO
);

  wire adder_1_cout, and_1_out, and_2_out, decoder_1_out0, decoder_1_out1, decoder_1_out2, decoder_1_out3,
       decoder_1_out4, decoder_1_out5, decoder_1_out6, decoder_1_out7, not_2_out, subtractor_1_bout;
  wire [3:0] adder_1_out, controlled_buffer_7_out, not_1_out, or_2_out, shifter_1_out, shifter_2_out,
       subtractor_1_out;

  or or_1 (OVERFLOW, and_1_out, and_2_out);
  and and_1 (and_1_out, adder_1_cout, decoder_1_out1);
  and and_2 (and_2_out, subtractor_1_bout, decoder_1_out2);
  assign \SAÍDA  = decoder_1_out0 ? B : 4'bz;  // Controlled_Buffer controlled_buffer_1
  Decoder #(.select(3)) decoder_1 (
    .out0(decoder_1_out0), .out1(decoder_1_out1), .out2(decoder_1_out2), .out3(decoder_1_out3),
    .out4(decoder_1_out4), .out5(decoder_1_out5), .out6(decoder_1_out6), .out7(decoder_1_out7),
    .sel(\OPERAÇÃO ));  // open: en
  Adder #(.width(4)) adder_1 (.a(A), .b(B), .out(adder_1_out), .cout(adder_1_cout));  // open: cin
  assign \SAÍDA  = decoder_1_out1 ? adder_1_out : 4'bz;  // Controlled_Buffer controlled_buffer_2
  Subtractor #(.width(4)) subtractor_1 (.a(A), .b(B), .out(subtractor_1_out), .bout(subtractor_1_bout));  // open: bin
  assign \SAÍDA  = decoder_1_out2 ? subtractor_1_out : 4'bz;  // Controlled_Buffer controlled_buffer_3
  nor nor_1 (ZERO, decoder_1_out7, decoder_1_out6, \SAÍDA [3], \SAÍDA [2], \SAÍDA [1], \SAÍDA [0]);
  assign not_1_out = ~B;  // NOT_Gate not_1, 4 bits wide
  assign or_2_out = A | B;  // OR_Gate or_2, 4 bits wide
  assign \SAÍDA  = decoder_1_out3 ? or_2_out : 4'bz;  // Controlled_Buffer controlled_buffer_4
  assign \SAÍDA  = decoder_1_out4 ? not_1_out : 4'bz;  // Controlled_Buffer controlled_buffer_5
  assign \SAÍDA  = decoder_1_out5 ? controlled_buffer_7_out : 4'bz;  // Controlled_Buffer controlled_buffer_6
  Shifter #(.width(4), .shift("lr")) shifter_1 (.in(B), .\dist (A[1:0]), .out(shifter_1_out));
  assign controlled_buffer_7_out = DIR ? shifter_1_out : 4'bz;  // Controlled_Buffer controlled_buffer_7
  not not_2 (not_2_out, DIR);
  Shifter #(.width(4)) shifter_2 (.in(B), .\dist (A[1:0]), .out(shifter_2_out));
  assign controlled_buffer_7_out = not_2_out ? shifter_2_out : 4'bz;  // Controlled_Buffer controlled_buffer_8
endmodule

module Desafio_display (
  input  in_1,
  input  in_2,
  input  in_3,
  input  in_4,
  input  in_5,
  input  in_6,
  input  in_7,
  input  in_8,
  input  in_9,
  input  in_10,
  input  in_11,
  input  in_12,
  input  in_13,
  input  in_14,
  input  in_15,
  input  in_16
);

  wire clock_1_out, not_1_out;
  wire [2:0] counter_1_q;
  wire [7:0] ram_1_data;

  Clock clock_1 (.out(clock_1_out));
  Counter #(.width(3), .max('h7)) counter_1 (.Q(counter_1_q), .clk(clock_1_out));  // open: load, D, count, carry, clr
  RAM #(.addrWidth(3)) ram_1 (.addr(counter_1_q), .data(ram_1_data), .clk(clock_1_out), .ld(in_1));  // open: sel, clr
  assign ram_1_data = not_1_out ? {1'b0, in_13, in_11, in_10, in_12, in_15, in_16, in_14} : 8'bz;  // Controlled_Buffer controlled_buffer_1
  not not_1 (not_1_out, in_1);
  _7_Segment_Display u_7_segment_display_1 (
    .g(ram_1_data[6]), .f(ram_1_data[5]), .a(ram_1_data[4]), .b(ram_1_data[3]), .e(ram_1_data[0]),
    .d(ram_1_data[1]), .c(ram_1_data[2]));  // open: dp
  _7_Segment_Display u_7_segment_display_2 (
    .g(in_3), .f(in_4), .a(in_5), .b(in_6), .e(in_9), .d(in_8), .c(in_7));  // open: dp
endmodule

module UC (
  input  [7:0] \Instrução ,
  input  CLK,
  input  RST,
  input  C,
  input  Z,
  output PC_RST,
  output IR,
  output PC,
  output AC,
  output RAM,
  output [3:0] Endereco,
  output [3:0] Operando,
  output \Mod__Endereçamento ,
  output [2:0] OpCode,
  output R_W,
  output Load
);

  wire GOTO_out, JC_out, JZ_out;
  wire [1:0] counter_1_q;

  Counter #(.width(2), .max('h3)) counter_1 (.Q(counter_1_q), .clk(CLK), .clr(RST));  // open: load, D, count, carry
  and and_1 (IR, ~counter_1_q[1], ~counter_1_q[0]);  // AND_Gate
  and and_2 (PC, ~counter_1_q[1], counter_1_q[0]);  // AND_Gate
  and and_3 (AC, counter_1_q[1], ~counter_1_q[0]);  // AND_Gate
  and GOTO (GOTO_out, \Instrução [7], \Instrução [6], \Instrução [5], ~\Instrução [4], IR);  // AND_Gate
  and and_4 (RAM, counter_1_q[1], counter_1_q[0]);
  and JC (JC_out, \Instrução [7], \Instrução [6], ~\Instrução [5], ~\Instrução [4], C, IR);  // AND_Gate
  or or_1 (Load, GOTO_out, JC_out, JZ_out);
  and JZ (JZ_out, \Instrução [7], \Instrução [6], ~\Instrução [5], ~\Instrução [4], Z, IR);  // AND_Gate
  nand nand_1 (R_W, AC, \Instrução [4], \Instrução [5], \Instrução [6], \Instrução [7]);

  assign Endereco = \Instrução [3:0];
  assign \Mod__Endereçamento  = \Instrução [4];
  assign OpCode = \Instrução [7:5];
  assign Operando = \Instrução [3:0];
  assign PC_RST = RST;
endmodule
