// Logisim project digital-timer-logisim.circ as structural Verilog: 6 circuits, main circuit main
module main (
);

  wire CLK, clock_1_out, comparador_2e4_1_out_3, cont_0a5_2_pulse, cont_0a5_3_pulse, cont_0a9_1_pulse,
       cont_0a9_2_pulse, cont_0a9_3_pulse, j_k_ff_1_q, ON, or_1_out, RS;
  wire [3:0] h1, h2, m1, m2, s1, s2;

  Button Iniciar___Pausar (.out(ON));
  Button Resetar (.out(RS));
  J_K_Flip_Flop j_k_ff_1 (.J(1'b1), .clk(ON), .K(1'b1), .Q(j_k_ff_1_q));  // open: Qn, preset, en, reset
  Hex_Digit_Display hex_digit_display_1 (.value(h2));  // open: dp
  Clock clock_1 (.out(clock_1_out));
  and and_1 (CLK, j_k_ff_1_q, clock_1_out);
  Hex_Digit_Display hex_digit_display_2 (.value(m2));  // open: dp
  Hex_Digit_Display hex_digit_display_3 (.value(h1));  // open: dp
  cont_0a5 cont_0a5_1 (.CLK(cont_0a9_1_pulse), .comparador(or_1_out), .out_3(h2));  // open: pulse
  Hex_Digit_Display hex_digit_display_4 (.value(m1));  // open: dp
  cont_0a9 cont_0a9_1 (.CLK(cont_0a5_2_pulse), .comparador(or_1_out), .pulse(cont_0a9_1_pulse), .out_3(h1));
  Hex_Digit_Display hex_digit_display_5 (.value(s2));  // open: dp
  Hex_Digit_Display hex_digit_display_6 (.value(s1));  // open: dp
  comparador_2e4 comparador_2e4_1 (.n1(h2), .n2(h1), .out_3(comparador_2e4_1_out_3));
  or or_1 (or_1_out, comparador_2e4_1_out_3, RS);
  cont_0a5 cont_0a5_2 (.CLK(cont_0a9_2_pulse), .comparador(or_1_out), .pulse(cont_0a5_2_pulse), .out_3(m2));
  cont_0a9 cont_0a9_2 (.CLK(cont_0a5_3_pulse), .comparador(or_1_out), .pulse(cont_0a9_2_pulse), .out_3(m1));
  cont_0a5 cont_0a5_3 (.CLK(cont_0a9_3_pulse), .comparador(or_1_out), .pulse(cont_0a5_3_pulse), .out_3(s2));
  cont_0a9 cont_0a9_3 (.CLK(CLK), .comparador(or_1_out), .pulse(cont_0a9_3_pulse), .out_3(s1));
endmodule

// 0-9
module cont_0a9 (
  input  CLK,
  input  comparador,
  output [3:0] out_3,
  output pulse
);

  wire or_1_out;

  J_K_Flip_Flop #(.trigger("falling")) j_k_ff_1 (
    .J(1'b1), .clk(CLK), .K(1'b1), .Q(out_3[0]), .reset(or_1_out));  // open: Qn, preset, en
  or or_1 (or_1_out, pulse, comparador);
  J_K_Flip_Flop #(.trigger("falling")) j_k_ff_2 (
    .J(1'b1), .clk(out_3[0]), .K(1'b1), .Q(out_3[1]), .reset(or_1_out));  // open: Qn, preset, en
  and and_1 (pulse, out_3[3], ~out_3[2], out_3[1], ~out_3[0]);  // AND_Gate
  J_K_Flip_Flop #(.trigger("falling")) j_k_ff_3 (
    .J(1'b1), .clk(out_3[1]), .K(1'b1), .Q(out_3[2]), .reset(or_1_out));  // open: Qn, preset, en
  J_K_Flip_Flop #(.trigger("falling")) j_k_ff_4 (
    .J(1'b1), .clk(out_3[2]), .K(1'b1), .Q(out_3[3]), .reset(or_1_out));  // open: Qn, preset, en

  // Notes on the sheet:
  //   Entrada para, quando o comando de resetar vier da main, zerar o contador.
endmodule

// 0-5
module cont_0a5 (
  input  CLK,
  input  comparador,
  output [3:0] out_3,
  output pulse
);

  wire or_1_out;

  J_K_Flip_Flop #(.trigger("falling")) j_k_ff_1 (
    .J(1'b1), .clk(CLK), .K(1'b1), .Q(out_3[0]), .reset(or_1_out));  // open: Qn, preset, en
  or or_1 (or_1_out, pulse, comparador);
  J_K_Flip_Flop #(.trigger("falling")) j_k_ff_2 (
    .J(1'b1), .clk(out_3[0]), .K(1'b1), .Q(out_3[1]), .reset(or_1_out));  // open: Qn, preset, en
  and and_1 (pulse, ~out_3[3], out_3[2], out_3[1], ~out_3[0]);  // AND_Gate
  J_K_Flip_Flop #(.trigger("falling")) j_k_ff_3 (
    .J(1'b1), .clk(out_3[1]), .K(1'b1), .Q(out_3[2]), .reset(or_1_out));  // open: Qn, preset, en
  J_K_Flip_Flop #(.trigger("falling")) j_k_ff_4 (
    .J(1'b1), .clk(out_3[2]), .K(1'b1), .Q(out_3[3]), .reset(or_1_out));  // open: Qn, preset, en

  // Notes on the sheet:
  //   Entrada para, quando o comando de resetar vier da main, zerar o contador.
endmodule

// comp1
module comparador_2e4 (
  input  [3:0] n1,
  input  [3:0] n2,
  output out_3
);

  wire and_1_out, and_2_out;

  and and_1 (and_1_out, ~n1[0], n1[1], ~n1[2], ~n1[3]);  // AND_Gate
  and and_2 (and_2_out, ~n2[0], ~n2[1], n2[2], ~n2[3]);  // AND_Gate
  and and_3 (out_3, and_1_out, and_2_out);

  // Notes on the sheet:
  //   Entrada para o 2 (0010)
  //   Entrada para o 4 (0100)
  //   Circuito para identificar quando entrar 2 e 4, negando os 0 e deixando sair verdade quando der 1111
endmodule

module relogio (
);

  wire CLK, clock_1_out, comparador_2e4_1_out_3, cont_0a5_2_pulse, cont_0a5_3_pulse, cont_0a9_1_pulse,
       cont_0a9_2_pulse, cont_0a9_3_pulse, j_k_ff_1_q, ON, undriven;
  wire [3:0] h1, h2, m1, m2, s1, s2;

  Button Iniciar___Pausar (.out(ON));
  J_K_Flip_Flop j_k_ff_1 (
    .J(1'b1), .clk(ON), .K(1'b1), .Q(j_k_ff_1_q), .en(undriven), .reset(undriven));  // open: Qn, preset
  Hex_Digit_Display hex_digit_display_1 (.value(h2));  // open: dp
  Clock clock_1 (.out(clock_1_out));
  and and_1 (CLK, j_k_ff_1_q, clock_1_out);
  Hex_Digit_Display hex_digit_display_2 (.value(h1));  // open: dp
  Hex_Digit_Display hex_digit_display_3 (.value(m2));  // open: dp
  cont_0a5 cont_0a5_1 (.CLK(cont_0a9_1_pulse), .comparador(comparador_2e4_1_out_3), .out_3(h2));  // open: pulse
  Hex_Digit_Display hex_digit_display_4 (.value(m1));  // open: dp
  cont_0a9 cont_0a9_1 (
    .CLK(cont_0a5_2_pulse), .comparador(comparador_2e4_1_out_3), .pulse(cont_0a9_1_pulse), .out_3(h1));
  Hex_Digit_Display hex_digit_display_5 (.value(s1));  // open: dp
  Hex_Digit_Display hex_digit_display_6 (.value(s2));  // open: dp
  comparador_2e4 comparador_2e4_1 (.n1(h2), .n2(h1), .out_3(comparador_2e4_1_out_3));
  cont_0a5 cont_0a5_2 (
    .CLK(cont_0a9_2_pulse), .comparador(comparador_2e4_1_out_3), .pulse(cont_0a5_2_pulse), .out_3(m2));
  cont_0a9 cont_0a9_2 (
    .CLK(cont_0a5_3_pulse), .comparador(comparador_2e4_1_out_3), .pulse(cont_0a9_2_pulse), .out_3(m1));
  cont_0a5 cont_0a5_3 (
    .CLK(cont_0a9_3_pulse), .comparador(comparador_2e4_1_out_3), .pulse(cont_0a5_3_pulse), .out_3(s2));
  cont_0a9 cont_0a9_3 (.CLK(CLK), .comparador(comparador_2e4_1_out_3), .pulse(cont_0a9_3_pulse), .out_3(s1));

  // Notes on the sheet:
  //   Controle da função iniciar e pausar, por meio do botão
  //   Identificar quando der 2 e 4
  //   para zerar o circuito
endmodule

module cronometro (
);

  wire CLK, clock_1_out, comparador_2e4_1_out_3, cont_0a5_2_pulse, cont_0a5_3_pulse, cont_0a9_1_pulse,
       cont_0a9_2_pulse, cont_0a9_3_pulse, j_k_ff_1_q, ON, or_1_out, RS;
  wire [3:0] h1, h2, m1, m2, s1, s2;

  Button Iniciar___Pausar (.out(ON));
  Button Resetar (.out(RS));
  J_K_Flip_Flop j_k_ff_1 (.J(1'b1), .clk(ON), .K(1'b1), .Q(j_k_ff_1_q));  // open: Qn, preset, en, reset
  Hex_Digit_Display hex_digit_display_1 (.value(h2));  // open: dp
  Clock clock_1 (.out(clock_1_out));
  and and_1 (CLK, j_k_ff_1_q, clock_1_out);
  Hex_Digit_Display hex_digit_display_2 (.value(h1));  // open: dp
  Hex_Digit_Display hex_digit_display_3 (.value(m2));  // open: dp
  cont_0a5 cont_0a5_1 (.CLK(cont_0a9_1_pulse), .comparador(or_1_out), .out_3(h2));  // open: pulse
  Hex_Digit_Display hex_digit_display_4 (.value(m1));  // open: dp
  cont_0a9 cont_0a9_1 (.CLK(cont_0a5_2_pulse), .comparador(or_1_out), .pulse(cont_0a9_1_pulse), .out_3(h1));
  Hex_Digit_Display hex_digit_display_5 (.value(s2));  // open: dp
  Hex_Digit_Display hex_digit_display_6 (.value(s1));  // open: dp
  comparador_2e4 comparador_2e4_1 (.n1(h2), .n2(h1), .out_3(comparador_2e4_1_out_3));
  or or_1 (or_1_out, comparador_2e4_1_out_3, RS);
  cont_0a5 cont_0a5_2 (.CLK(cont_0a9_2_pulse), .comparador(or_1_out), .pulse(cont_0a5_2_pulse), .out_3(m2));
  cont_0a9 cont_0a9_2 (.CLK(cont_0a5_3_pulse), .comparador(or_1_out), .pulse(cont_0a9_2_pulse), .out_3(m1));
  cont_0a5 cont_0a5_3 (.CLK(cont_0a9_3_pulse), .comparador(or_1_out), .pulse(cont_0a5_3_pulse), .out_3(s2));
  cont_0a9 cont_0a9_3 (.CLK(CLK), .comparador(or_1_out), .pulse(cont_0a9_3_pulse), .out_3(s1));

  // Notes on the sheet:
  //   Opção para resetar o circuito pelo botão
endmodule
